// Logisim project sistema-semaforico-avanzato.circ as structural Verilog: 7 circuits, main circuit main
module main (
);

  wire clock, N, P, pedestrians_timer_1_dot, plus_h, plus_m;
  wire [2:0] A, B, C, D;
  wire [3:0] h0, h1, m0, m1, pedestrians_timer_1_display;

  Clock clock_1 (.out(clock));
  digital_clock digital_clock_1 (
    .H1(h1), .H0(h0), .M1(m1), .M0(m0), .night_mode(N), .CLK(clock), .plus_H(plus_h), .plus_M(plus_m));
  controller controller_1 (.Clock(clock), .A(A), .B(B), .C(C), .D(D), .activate_timer(P), .Night_mode(N));
  LED led_1 (.in(A[0]));
  LED led_2 (.in(A[1]));
  LED led_3 (.in(A[2]));
  Hex_Digit_Display hex_digit_display_1 (.value(h1));  // open: dp
  LED led_4 (.in(B[0]));
  LED led_5 (.in(B[1]));
  LED led_6 (.in(B[2]));
  Hex_Digit_Display hex_digit_display_2 (.value(h0));  // open: dp
  LED led_7 (.in(C[0]));
  LED led_8 (.in(C[1]));
  LED led_9 (.in(C[2]));
  Hex_Digit_Display hex_digit_display_3 (.value(m1));  // open: dp
  Hex_Digit_Display hex_digit_display_4 (.value(m0));  // open: dp
  Button button_1 (.out(plus_h));
  Button button_2 (.out(plus_m));
  LED led_10 (.in(D[0]));
  LED led_11 (.in(D[1]));
  LED led_12 (.in(D[2]));
  LED led_13 (.in(N));
  Hex_Digit_Display hex_digit_display_5 (.value(pedestrians_timer_1_display), .dp(pedestrians_timer_1_dot));
  pedestrians_timer pedestrians_timer_1 (
    .active(P), .display(pedestrians_timer_1_display), .clock(clock), .dot(pedestrians_timer_1_dot));

  // Notes on the sheet:
  //   La modalità notte è attiva
  //   dalle ore 23 alle ore 6 (comprese)
  //   Sistema semaforico avanzato
  //   Progetto d'esame di Architettura degli Elaboratori I
  //   Marco Aceti <marco.aceti@studenti.unimi.it>
  //   Orario attuale
  //   Regola orologio
  //   +1 ora
  //   +1 minuto
  //   Modalità notturna
  //   display pedoni
endmodule

module loop_counter (
  input  clock,
  output [6:0] out_2
);

  wire comparator_1_lt;

  Counter #(.width(7), .max('h7f)) counter_1 (
    .Q(out_2), .clk(clock), .clr(comparator_1_lt));  // open: load, D, count, carry
  Comparator #(.width(7), .mode("unsigned")) comparator_1 (
    .a(7'b1101100), .b(out_2), .lt(comparator_1_lt));  // open: gt, eq
endmodule

module state_selector (
  input  clock,
  output _1,
  output _2,
  output _3,
  output _4,
  output _5,
  output _6,
  output _7,
  output _8,
  output _9,
  output _10,
  output _11,
  output _12
);

  wire comparator_1_eq, comparator_1_gt, comparator_1_lt, comparator_2_eq, comparator_2_lt, comparator_3_gt,
       comparator_4_eq, comparator_4_gt, comparator_4_lt, comparator_5_eq, comparator_5_lt, comparator_6_gt,
       comparator_7_eq, comparator_7_gt, comparator_7_lt, comparator_8_eq, comparator_8_lt, comparator_9_gt,
       comparator_10_eq, comparator_10_gt, comparator_10_lt, comparator_11_eq, comparator_11_lt, or_2_out,
       or_3_out, or_4_out, or_5_out, or_6_out, or_7_out, or_8_out;
  wire [6:0] loop_counter_1_out_2;

  loop_counter loop_counter_1 (.out_2(loop_counter_1_out_2), .clock(clock));
  Comparator #(.width(7), .mode("unsigned")) comparator_1 (
    .a(loop_counter_1_out_2), .b(7'b0010011), .gt(comparator_1_gt), .eq(comparator_1_eq), .lt(comparator_1_lt));
  Comparator #(.width(7), .mode("unsigned")) comparator_2 (
    .a(loop_counter_1_out_2), .b(7'b0010111), .eq(comparator_2_eq), .lt(comparator_2_lt));  // open: gt
  Comparator #(.width(7), .mode("unsigned")) comparator_3 (
    .a(loop_counter_1_out_2), .b(7'b0011000), .gt(comparator_3_gt), .eq(_3));  // open: lt
  Comparator #(.width(7), .mode("unsigned")) comparator_4 (
    .a(loop_counter_1_out_2), .b(7'b0101100), .gt(comparator_4_gt), .eq(comparator_4_eq), .lt(comparator_4_lt));
  Comparator #(.width(7), .mode("unsigned")) comparator_5 (
    .a(loop_counter_1_out_2), .b(7'b0110000), .eq(comparator_5_eq), .lt(comparator_5_lt));  // open: gt
  Comparator #(.width(7), .mode("unsigned")) comparator_6 (
    .a(loop_counter_1_out_2), .b(7'b0110001), .gt(comparator_6_gt), .eq(_6));  // open: lt
  Comparator #(.width(7), .mode("unsigned")) comparator_7 (
    .a(loop_counter_1_out_2), .b(7'b1011001), .gt(comparator_7_gt), .eq(comparator_7_eq), .lt(comparator_7_lt));
  Comparator #(.width(7), .mode("unsigned")) comparator_8 (
    .a(loop_counter_1_out_2), .b(7'b1011101), .eq(comparator_8_eq), .lt(comparator_8_lt));  // open: gt
  Comparator #(.width(7), .mode("unsigned")) comparator_9 (
    .a(loop_counter_1_out_2), .b(7'b1011110), .gt(comparator_9_gt), .eq(_9));  // open: lt
  Comparator #(.width(7), .mode("unsigned")) comparator_10 (
    .a(loop_counter_1_out_2), .b(7'b1100111), .gt(comparator_10_gt), .eq(comparator_10_eq),
    .lt(comparator_10_lt));
  Comparator #(.width(7), .mode("unsigned")) comparator_11 (
    .a(loop_counter_1_out_2), .b(7'b1101011), .eq(comparator_11_eq), .lt(comparator_11_lt));  // open: gt
  Comparator #(.width(7), .mode("unsigned")) comparator_12 (
    .a(loop_counter_1_out_2), .b(7'b1101100), .eq(_12));  // open: gt, lt
  or or_1 (_1, comparator_1_eq, comparator_1_lt);
  and and_1 (_2, comparator_1_gt, or_2_out);
  or or_2 (or_2_out, comparator_2_eq, comparator_2_lt);
  and and_2 (_4, comparator_3_gt, or_3_out);
  or or_3 (or_3_out, comparator_4_eq, comparator_4_lt);
  and and_3 (_5, comparator_4_gt, or_4_out);
  or or_4 (or_4_out, comparator_5_eq, comparator_5_lt);
  and and_4 (_7, comparator_6_gt, or_5_out);
  or or_5 (or_5_out, comparator_7_eq, comparator_7_lt);
  and and_5 (_8, comparator_7_gt, or_6_out);
  or or_6 (or_6_out, comparator_8_eq, comparator_8_lt);
  and and_6 (_10, comparator_9_gt, or_7_out);
  or or_7 (or_7_out, comparator_10_eq, comparator_10_lt);
  and and_7 (_11, comparator_10_gt, or_8_out);
  or or_8 (or_8_out, comparator_11_eq, comparator_11_lt);
endmodule

module controller (
  input  Clock,
  input  Night_mode,
  output [2:0] A,
  output [2:0] B,
  output [2:0] C,
  output [2:0] D,
  output activate_timer
);

  wire and_1_out, or_1_out, state_selector_1__1, state_selector_1__2, state_selector_1__4,
       state_selector_1__5, state_selector_1__7, state_selector_1__8, state_selector_1__10,
       state_selector_1__11;

  and and_1 (and_1_out, ~Night_mode, Clock);  // AND_Gate
  state_selector state_selector_1 (
    .clock(and_1_out), ._1(state_selector_1__1), ._2(state_selector_1__2), ._4(state_selector_1__4),
    ._5(state_selector_1__5), ._7(state_selector_1__7), ._8(state_selector_1__8), ._10(state_selector_1__10),
    ._11(state_selector_1__11));  // open: _3, _6, _9, _12
  or or_1 (or_1_out, state_selector_1__11, state_selector_1__10);
  semaphore semaphore_1 (
    .green_in(state_selector_1__1), .yellow_in(state_selector_1__2), .green_out(A[2]), .yellow_out(A[1]),
    .red_out(A[0]), .night_mode(Night_mode), .clock(Clock));
  semaphore semaphore_2 (
    .green_in(state_selector_1__4), .yellow_in(state_selector_1__5), .green_out(B[2]), .yellow_out(B[1]),
    .red_out(B[0]), .night_mode(Night_mode), .clock(Clock));
  semaphore semaphore_3 (
    .green_in(state_selector_1__7), .yellow_in(state_selector_1__8), .green_out(C[2]), .yellow_out(C[1]),
    .red_out(C[0]), .night_mode(Night_mode), .clock(Clock));
  semaphore semaphore_4 (
    .green_in(state_selector_1__10), .yellow_in(state_selector_1__11), .green_out(D[2]), .yellow_out(D[1]),
    .red_out(D[0]), .night_mode(Night_mode), .clock(Clock));
  and and_2 (activate_timer, ~Night_mode, or_1_out);  // AND_Gate
endmodule

module semaphore (
  input  green_in,
  input  yellow_in,
  input  night_mode,
  input  clock,
  output red_out,
  output green_out,
  output yellow_out
);

  wire and_2_out, and_3_out, comparator_1_lt;
  wire [2:0] counter_1_q;

  and and_1 (green_out, green_in, ~night_mode);  // AND_Gate
  and and_2 (and_2_out, yellow_in, ~night_mode);  // AND_Gate
  Counter #(.width(3), .max('h7)) counter_1 (.Q(counter_1_q), .clk(clock));  // open: load, D, count, carry, clr
  and and_3 (and_3_out, night_mode, comparator_1_lt);
  Comparator #(.width(3), .mode("unsigned")) comparator_1 (
    .a(counter_1_q), .b(3'b100), .lt(comparator_1_lt));  // open: gt, eq
  nor nor_1 (red_out, night_mode, and_2_out, green_out);
  or or_1 (yellow_out, and_2_out, and_3_out);
endmodule

module pedestrians_timer (
  input  active,
  input  clock,
  output [3:0] display,
  output dot
);

  wire not_1_out;
  wire [0:0] comparator_1_lt;
  wire [3:0] counter_1_q, not_2_out, subtractor_1_out;

  Counter #(.width(4), .max('hf)) counter_1 (
    .Q(counter_1_q), .clk(clock), .clr(not_1_out));  // open: load, D, count, carry
  not not_1 (not_1_out, active);
  Comparator #(.width(4), .mode("unsigned")) comparator_1 (
    .a(4'b1001), .b(counter_1_q), .lt(comparator_1_lt[0]));  // open: gt, eq
  assign not_2_out = ~counter_1_q;  // NOT_Gate not_2, 4 bits wide
  Subtractor #(.width(4)) subtractor_1 (.a(not_2_out), .b(4'b0110), .out(subtractor_1_out));  // open: bin, bout
  Multiplexer #(.select(2), .width(4)) multiplexer_1 (
    .in2(subtractor_1_out), .in3(4'b0000), .out(display), .sel({active, comparator_1_lt[0]}));  // open: in0, in1, en
  and and_1 (dot, comparator_1_lt[0], ~counter_1_q[0]);  // AND_Gate
endmodule

module digital_clock (
  input  CLK,
  input  plus_H,
  input  plus_M,
  output [3:0] H1,
  output [3:0] H0,
  output [3:0] M1,
  output [3:0] M0,
  output night_mode
);

  wire and_1_out, and_2_out, and_3_out, and_4_out, comparator_1_gt, comparator_2_eq, comparator_2_gt,
       comparator_3_eq, comparator_3_lt, counter_2_carry, counter_3_carry, counter_4_carry, counter_5_carry,
       counter_6_carry, or_1_out, or_2_out, or_3_out, or_5_out;
  wire [3:0] counter_5_q, counter_6_q;

  Comparator #(.mode("unsigned")) comparator_1 (.a({H1, H0}), .b(8'h23), .gt(comparator_1_gt));  // open: eq, lt
  and and_1 (and_1_out, counter_2_carry, or_3_out);
  or or_1 (or_1_out, comparator_2_gt, comparator_2_eq);
  Comparator #(.mode("unsigned")) comparator_2 (
    .a({H1, H0}), .b(8'h22), .gt(comparator_2_gt), .eq(comparator_2_eq));  // open: lt
  Comparator #(.mode("unsigned")) comparator_3 (
    .a({H1, H0}), .b(8'h6), .eq(comparator_3_eq), .lt(comparator_3_lt));  // open: gt
  or or_2 (or_2_out, comparator_3_eq, comparator_3_lt);
  Hex_Digit_Display hex_digit_display_1 (.value(H1));  // open: dp
  Counter #(.width(4), .max('h2)) counter_1 (
    .count(and_1_out), .Q(H1), .clk(CLK), .clr(comparator_1_gt));  // open: load, D, carry
  and and_2 (and_2_out, and_3_out, counter_3_carry);
  or or_3 (or_3_out, and_2_out, plus_H);
  Hex_Digit_Display hex_digit_display_2 (.value(H0));  // open: dp
  Counter #(.width(4), .max('h9)) counter_2 (
    .count(or_3_out), .Q(H0), .carry(counter_2_carry), .clk(CLK), .clr(comparator_1_gt));  // open: load, D
  and and_3 (and_3_out, counter_4_carry, or_5_out);
  LED led_1 (.in(night_mode));
  or or_4 (night_mode, or_1_out, or_2_out);
  Hex_Digit_Display hex_digit_display_3 (.value(M1));  // open: dp
  Counter #(.width(4), .max('h5)) counter_3 (
    .count(and_3_out), .Q(M1), .carry(counter_3_carry), .clk(CLK));  // open: load, D, clr
  or or_5 (or_5_out, and_4_out, plus_M);
  Hex_Digit_Display hex_digit_display_4 (.value(M0));  // open: dp
  Counter #(.width(4), .max('h9)) counter_4 (
    .count(or_5_out), .Q(M0), .carry(counter_4_carry), .clk(CLK));  // open: load, D, clr
  and and_4 (and_4_out, counter_6_carry, counter_5_carry);
  Hex_Digit_Display hex_digit_display_5 (.value(counter_5_q));  // open: dp
  Counter #(.width(4), .max('h5)) counter_5 (
    .count(counter_6_carry), .Q(counter_5_q), .carry(counter_5_carry), .clk(CLK));  // open: load, D, clr
  Counter #(.width(4), .max('h9)) counter_6 (
    .Q(counter_6_q), .carry(counter_6_carry), .clk(CLK));  // open: load, D, count, clr
  Hex_Digit_Display hex_digit_display_6 (.value(counter_6_q));  // open: dp

  // Notes on the sheet:
  //   ore
  //   minuti
  //   secondi
endmodule
